# Fritzing sketch light_stick (saved by Fritzing 0.9.3b)
breadboards: 1

parts:
  U1 = ESP8266 NodeMCU LoLin module
  LED_3_9 = ws2812b [package="smd 2812b"]
  S1 = Pushbutton [package="[THT]"]

nets:
  N1: U1.D1, S1.Pin_1, S1.Pin_2
  N2: U1.D6, LED_3_9.DIN
  GND: U1.GND, LED_3_9.VSS, S1.Pin_3, S1.Pin_4
  N3: U1.VU, LED_3_9.VDD

custom parts:
  ESP8266 NodeMCU LoLin module: ESP8266 based NodeMCU
